# Fritzing sketch Daningsih05 (saved by Fritzing 0.8.7b)
breadboards: 1

parts:
  LED1 = LED - 5mm [color="Red (633nm)" package="5 mm [THT]"]
  LED2 = LED - 5mm [color="Yellow (595nm)" package="5 mm [THT]"]
  LED3 = LED - 5mm [color="Green (565nm)" package="5 mm [THT]"]
  T1 = LM35 Temperature Sensor [package="TO92 [THT]"]
  R1 = Resistor [tolerance=±5% resistance=220 package=THT]
  R2 = Resistor [tolerance=±5% resistance=220 package=THT]
  R3 = Resistor [tolerance=±5% resistance=220 package=THT]
  Part1 = Arduino Uno (Rev3)

nets:
  N1: LED1.cathode, R1.Pin_1
  N2: LED1.anode, Part1.D4
  N3: LED2.cathode, R2.Pin_1
  N4: LED2.anode, Part1.D3_PWM
  N5: LED3.cathode, R3.Pin_1
  N6: LED3.anode, Part1.D2
  N7: T1.+Vs, Part1.5V
  N8: T1.Vout, Part1.A0
  GND: T1.GND, Part1.GND
  N9: R1.Pin_0, R2.Pin_0, R3.Pin_0
